// Digital circuit 1.dig as structural Verilog
module _1 (
  input  A,
  input  B,
  input  S,
  output Y
);

  wire and_1_out, and_2_out, not_1_out;

  not not_1 (not_1_out, S);
  and and_1 (and_1_out, A, not_1_out);
  and and_2 (and_2_out, B, S);
  or or_1 (Y, and_1_out, and_2_out);
endmodule
