// Digital circuit TransformarAC2toASM.dig as structural Verilog
module TransformarAC2toASM (
  input  A0,
  input  A1,
  input  A2,
  output R0,
  output R1,
  output R2,
  output Cout
);

  wire fa_1_y, not_1_out, not_2_out;

  not not_1 (not_1_out, A0);
  not not_2 (not_2_out, A1);
  FA fa_1 (.A(not_1_out), .B(not_2_out), .Cin(1'b0), .Y(fa_1_y), .Cout(Cout));
  _2 _2_1 (.A0(A0), .A1(A1), .B0(fa_1_y), .B1(Cout), .S(A2), .Y0(R0), .Y1(R1));

  assign R2 = A2;
endmodule
