// Digital circuit solucio.dig as structural Verilog
module solucio (
  input  A0,
  input  A1,
  input  A2,
  input  B0,
  input  B1,
  input  B2,
  input  C0,
  input  C1,
  output R0,
  output R1,
  output R2
);

  wire alu_1_ovf, showdisplay_1_a, showdisplay_1_b, showdisplay_1_c, showdisplay_1_d, showdisplay_1_e,
       showdisplay_1_f, showdisplay_1_g, showdisplay_1_h, showdisplay_2_a, showdisplay_2_b, showdisplay_2_c,
       showdisplay_2_d, showdisplay_2_e, showdisplay_2_f, showdisplay_2_g, showdisplay_2_h, showdisplay_3_a,
       showdisplay_3_b, showdisplay_3_c, showdisplay_3_d, showdisplay_3_e, showdisplay_3_f, showdisplay_3_g,
       showdisplay_3_h;

  showDisplay showdisplay_1 (
    .X0(A0), .X1(A1), .X2(A2), .A(showdisplay_1_a), .B(showdisplay_1_b), .C(showdisplay_1_c),
    .D(showdisplay_1_d), .E(showdisplay_1_e), .F(showdisplay_1_f), .G(showdisplay_1_g), .H(showdisplay_1_h));
  showDisplay showdisplay_2 (
    .X0(B0), .X1(B1), .X2(B2), .A(showdisplay_2_a), .B(showdisplay_2_b), .C(showdisplay_2_c),
    .D(showdisplay_2_d), .E(showdisplay_2_e), .F(showdisplay_2_f), .G(showdisplay_2_g), .H(showdisplay_2_h));
  Seven_Seg seven_seg_1 (
    .a(showdisplay_1_a), .b(showdisplay_1_b), .c(showdisplay_1_c), .d(showdisplay_1_d), .e(showdisplay_1_e),
    .f(showdisplay_1_f), .g(showdisplay_1_g), .dp(showdisplay_1_h));
  ALU alu_1 (
    .A0(A0), .A1(A1), .A2(A2), .B0(B0), .B1(B1), .B2(B2), .C0(C0), .C1(C1), .R0(R0), .R1(R1), .R2(R2),
    .OVF(alu_1_ovf));
  Seven_Seg seven_seg_2 (
    .a(showdisplay_2_a), .b(showdisplay_2_b), .c(showdisplay_2_c), .d(showdisplay_2_d), .e(showdisplay_2_e),
    .f(showdisplay_2_f), .g(showdisplay_2_g), .dp(showdisplay_2_h));
  LED OVF (.in(alu_1_ovf));
  Seven_Seg seven_seg_3 (.a(1'b0), .b(1'b0), .c(1'b0), .d(1'b0), .e(1'b0), .f(1'b0), .g(alu_1_ovf), .dp(1'b0));
  showDisplay showdisplay_3 (
    .X0(R0), .X1(R1), .X2(R2), .A(showdisplay_3_a), .B(showdisplay_3_b), .C(showdisplay_3_c),
    .D(showdisplay_3_d), .E(showdisplay_3_e), .F(showdisplay_3_f), .G(showdisplay_3_g), .H(showdisplay_3_h));
  Seven_Seg seven_seg_4 (
    .a(showdisplay_3_a), .b(showdisplay_3_b), .c(showdisplay_3_c), .d(showdisplay_3_d), .e(showdisplay_3_e),
    .f(showdisplay_3_f), .g(showdisplay_3_g), .dp(showdisplay_3_h));
endmodule
