// Digital circuit J0.dig as structural Verilog
module J0 (
  input  X2,
  input  X1,
  input  X0,
  input  Q2,
  input  Q1,
  input  Q0,
  output J0
);

  wire and_1_out, and_2_out, not_5_out, not_6_out;

  // Not not_1 has open pins: in=Q2, out=open
  // Not not_2 has open pins: in=Q1, out=open
  // Not not_3 has open pins: in=Q0, out=open
  // Not not_4 has open pins: in=X2, out=open
  not not_5 (not_5_out, X1);
  not not_6 (not_6_out, X0);
  and and_1 (and_1_out, X1, not_6_out);
  and and_2 (and_2_out, Q1, not_5_out, X0);
  or or_1 (J0, and_1_out, and_2_out);

  // Notes on the sheet:
  //   X2: 0 ⇢ Manual
  //   1 ⇢ Automatic
endmodule
