// Digital circuit K2.dig as structural Verilog
module K2 (
  input  X2,
  input  X1,
  input  X0,
  input  Q2,
  input  Q1,
  input  Q0,
  output K2
);

  wire or_1_out;

  // Not not_1 has open pins: in=Q2, out=open
  // Not not_2 has open pins: in=Q1, out=open
  // Not not_3 has open pins: in=Q0, out=open
  // Not not_4 has open pins: in=X2, out=open
  // Not not_5 has open pins: in=X1, out=open
  // Not not_6 has open pins: in=X0, out=open
  or or_1 (or_1_out, X2, X1);
  and and_1 (K2, X0, or_1_out);

  // Notes on the sheet:
  //   X2: 0 ⇢ Manual
  //   1 ⇢ Automatic
endmodule
