// Digital circuit PL.dig as structural Verilog
module PL (
  input  X2,
  input  X1,
  input  X0,
  input  Q2,
  input  Q1,
  input  Q0,
  output PL
);

  wire and_1_out, and_2_out, not_3_out, not_4_out;

  // Not not_1 has open pins: in=X2, out=open
  // Not not_2 has open pins: in=X1, out=open
  not not_3 (not_3_out, X0);
  not not_4 (not_4_out, Q2);
  // Not not_5 has open pins: in=Q1, out=open
  // Not not_6 has open pins: in=Q0, out=open
  and and_1 (and_1_out, not_4_out, X1, X0);
  and and_2 (and_2_out, Q2, X1, not_3_out);
  or or_1 (PL, and_1_out, and_2_out);

  // Notes on the sheet:
  //   X2: 0 ⇢ Manual
  //   1 ⇢ Automatic
endmodule
